# Fritzing sketch xmas_tree_ball_fritz (saved by Fritzing 0.9.3b)
circuit board: 6cm x 4cm
breadboards: 1

parts:
  LED1 = LED - 5mm [color="Red (633nm)" package="5 mm [THT]"]
  LED2 = LED - 5mm [color="Red (633nm)" package="5 mm [THT]"]
  LED3 = LED - 5mm [color="Red (633nm)" package="5 mm [THT]"]
  LED4 = LED - 5mm [color="Red (633nm)" package="5 mm [THT]"]
  LED5 = LED - 5mm [color="Red (633nm)" package="5 mm [THT]"]
  C1 = Electrolytic Capacitor [capacitance=10µF package="100 mil [THT, electrolytic]"]
  C2 = Capacitor [package=cap-pth-small2]
  U1 = ATTINY13 [package=dip]
  BAT1 = Battery Holders [package=battcom_20mm_pth]

nets:
  N1: LED1.cathode, LED2.anode, LED3.anode, LED4.cathode, U1.PB3(ADC3)
  N2: LED1.anode, LED2.cathode, LED5.anode, U1.PB2(SCK_ADC1)
  N3: LED3.cathode, LED4.anode, LED5.cathode, U1.PB4(ADC2)
  N4: C1.-, C2.2, U1.GND, BAT1.-
  N5: C1.+, C2.1, U1.VCC, BAT1.+
